// Logisim project Circuitos.circ as structural Verilog: 1 circuit, main circuit main
module main (
  input  [2:0] Nota_2,
  input  Tom
);

  wire and_1_out, and_2_out, and_3_out, and_4_out, and_5_out, and_6_out, and_7_out, and_8_out, and_9_out,
       and_10_out, and_11_out, and_12_out, and_13_out, and_14_out, and_15_out, and_16_out, and_17_out,
       and_18_out, and_19_out, and_20_out, and_21_out, and_22_out, and_23_out, and_24_out, and_25_out,
       and_26_out, and_27_out, not_1_out, not_2_out, not_3_out, not_4_out, or_1_out, or_2_out, or_3_out,
       or_4_out, or_5_out, or_6_out, or_7_out, or_8_out, or_9_out, or_10_out;

  not not_1 (not_1_out, Nota_2[2]);
  not not_2 (not_2_out, Nota_2[1]);
  not not_3 (not_3_out, Nota_2[0]);
  not not_4 (not_4_out, Tom);
  or or_1 (or_1_out, Tom, not_4_out);
  and and_1 (and_1_out, not_1_out, not_2_out, not_3_out);
  and and_2 (and_2_out, not_2_out, not_3_out, Tom);
  and and_3 (and_3_out, not_1_out, Nota_2[0], not_4_out);
  and and_4 (and_4_out, Nota_2[1], Nota_2[0], not_4_out);
  and and_5 (and_5_out, not_1_out, not_2_out, not_3_out);
  and and_6 (and_6_out, Nota_2[2], Nota_2[1], not_3_out);
  and and_7 (and_7_out, not_1_out, Nota_2[1], Nota_2[0]);
  and and_8 (and_8_out, Nota_2[2], Nota_2[0], Tom);
  and and_9 (and_9_out, not_1_out, not_3_out);
  and and_10 (and_10_out, Nota_2[1], not_3_out);
  and and_11 (and_11_out, Nota_2[1], Tom);
  and and_12 (and_12_out, Nota_2[0], not_4_out);
  and and_13 (and_13_out, not_1_out, not_2_out);
  and and_14 (and_14_out, not_1_out, not_4_out);
  and and_15 (and_15_out, not_2_out, not_4_out);
  and and_16 (and_16_out, Nota_2[1], not_3_out, Tom);
  and and_17 (and_17_out, not_2_out, Nota_2[0], not_4_out);
  and and_18 (and_18_out, Nota_2[2], Nota_2[1], not_3_out);
  and and_19 (and_19_out, not_1_out, not_2_out);
  and and_20 (and_20_out, Nota_2[2], Nota_2[1], not_3_out, not_4_out);
  and and_21 (and_21_out, not_1_out, not_2_out, not_3_out);
  and and_22 (and_22_out, not_1_out, Nota_2[1], Nota_2[0]);
  and and_23 (and_23_out, Nota_2[2], not_2_out, Nota_2[0]);
  and and_24 (and_24_out, not_2_out, Tom);
  and and_25 (and_25_out, not_1_out, not_2_out, not_3_out);
  and and_26 (and_26_out, Nota_2[2], Nota_2[1], Nota_2[0]);
  and and_27 (and_27_out, Nota_2[2], not_2_out, not_4_out);
  or or_2 (or_2_out, and_1_out, Tom);
  or or_3 (or_3_out, and_2_out, and_3_out, and_4_out);
  or or_4 (or_4_out, and_5_out, and_6_out, and_7_out);
  or or_5 (or_5_out, and_8_out, and_9_out, and_10_out, and_11_out);
  or or_6 (or_6_out, and_12_out, and_13_out, and_14_out, and_15_out);
  or or_7 (or_7_out, and_16_out, and_17_out, and_18_out, and_19_out);
  or or_8 (or_8_out, and_20_out, and_21_out, and_22_out, and_23_out, and_24_out);
  or or_9 (or_9_out, and_25_out, and_26_out, and_27_out);
  or or_10 (or_10_out, or_3_out, or_4_out);
  _7_Segment_Display #(.active("false")) u_7_segment_display_1 (
    .g(or_9_out), .f(or_8_out), .a(or_2_out), .b(or_10_out), .e(or_7_out), .d(or_6_out), .c(or_5_out),
    .dp(or_1_out));

  // Notes on the sheet:
  //   A
  //   Nota 1
  //   B
  //   C
  //   D
  //   Nota 3
  //   D' +D
  //   A'B'C' + D
  //   S0
  //   ACD + A'C' + BC' + BD
  //   S2
  //   CD' + A'B' + A'D' + B'D'
  //   S3
  //   BC'D + B'CD' + ABC' + A'B'
  //   S4
  //   ABC'D' + A'B'C' + A'BC + AB'C + B'D
  //   A'B'C' + ABC + AB'D'
  //   B'C'D + A'CD' + BCD' + A'B'C' + ABC' + A'BC
  //   S1
  //   S5
  //   S6
  //   PONTO/NULO
endmodule
